// Logisim project Trabalho_final.circ as structural Verilog: 5 circuits, main circuit main
module main (
  input  A,
  input  B,
  input  in_3,
  input  C,
  input  D,
  input  in_6,
  input  in_7,
  input  in_8,
  input  in_9,
  input  in_10,
  input  in_11,
  input  in_12
);

  wire alvo_1_s1, alvo_1_s2, alvo_1_s3, alvo_1_s4, navio_1_1_bingo, navio_2_1_bingo, resultado_1_acertou,
       resultado_1_errou;

  Alvo alvo_1 (.A(A), .B(B), .C(C), .D(D), .S1(alvo_1_s1), .S2(alvo_1_s2), .S3(alvo_1_s3), .S4(alvo_1_s4));
  Navio_1 navio_1_1 (
    .A(alvo_1_s1), .NA(in_3), .B(alvo_1_s2), .NB(in_6), .C(alvo_1_s3), .NC(in_7), .D(alvo_1_s4), .ND(in_8),
    .bingo(navio_1_1_bingo));
  Navio_2 navio_2_1 (
    .A(alvo_1_s1), .NA(in_9), .B(alvo_1_s2), .NB(in_10), .C(alvo_1_s3), .NC(in_11), .D(alvo_1_s4),
    .ND(in_12), .bingo(navio_2_1_bingo));
  Resultado resultado_1 (
    .in_1(navio_1_1_bingo), .in_2(navio_2_1_bingo), .acertou(resultado_1_acertou), .errou(resultado_1_errou));
  LED led_1 ();  // open: in
  LED led_2 ();  // open: in
endmodule

module Alvo (
  input  A,
  input  B,
  input  C,
  input  D,
  output S1,
  output S2,
  output S3,
  output S4
);

  wire and_1_out, and_2_out, and_3_out, and_4_out, and_5_out, and_6_out, and_7_out, and_8_out, and_9_out,
       and_10_out, and_11_out, and_12_out, and_13_out, and_14_out, and_15_out, and_16_out, not_1_out,
       not_2_out, not_3_out, not_4_out;

  not not_1 (not_1_out, A);
  not not_2 (not_2_out, B);
  not not_3 (not_3_out, C);
  not not_4 (not_4_out, D);
  and and_1 (and_1_out, not_1_out, not_2_out, not_4_out);
  and and_2 (and_2_out, not_1_out, B, D);
  and and_3 (and_3_out, A, not_3_out, not_4_out);
  and and_4 (and_4_out, A, C, D);
  and and_5 (and_5_out, not_2_out, not_3_out, D);
  and and_6 (and_6_out, not_1_out, B, C, not_4_out);
  and and_7 (and_7_out, A, not_3_out);
  and and_8 (and_8_out, A, D);
  and and_9 (and_9_out, not_2_out, not_4_out);
  and and_10 (and_10_out, C, not_4_out);
  and and_11 (and_11_out, A, not_2_out, not_3_out);
  and and_12 (and_12_out, A, not_4_out);
  and and_13 (and_13_out, not_1_out, not_3_out, not_4_out);
  and and_14 (and_14_out, not_2_out, not_3_out);
  and and_15 (and_15_out, B, C, D);
  and and_16 (and_16_out, A, B, C);
  or or_1 (S1, and_1_out, and_2_out, and_3_out, and_4_out);
  or or_2 (S2, and_5_out, and_6_out, and_7_out, and_8_out);
  or or_3 (S3, and_9_out, and_10_out, and_11_out, and_12_out);
  or or_4 (S4, and_13_out, and_14_out, and_15_out, and_16_out);
endmodule

module Navio_1 (
  input  A,
  input  NA,
  input  B,
  input  NB,
  input  C,
  input  NC,
  input  D,
  input  ND,
  output bingo
);

  wire comparator_1_eq, comparator_2_eq, comparator_3_eq, comparator_4_eq;

  Comparator #(.width(1)) comparator_1 (.a(A), .b(NA), .eq(comparator_1_eq));  // open: gt, lt
  Comparator #(.width(1)) comparator_2 (.a(B), .b(NB), .eq(comparator_2_eq));  // open: gt, lt
  Comparator #(.width(1)) comparator_3 (.a(C), .b(NC), .eq(comparator_3_eq));  // open: gt, lt
  Comparator #(.width(1)) comparator_4 (.a(D), .b(ND), .eq(comparator_4_eq));  // open: gt, lt
  and and_1 (bingo, comparator_1_eq, comparator_2_eq, comparator_3_eq, comparator_4_eq);
endmodule

module Navio_2 (
  input  A,
  input  NA,
  input  B,
  input  NB,
  input  C,
  input  NC,
  input  D,
  input  ND,
  output bingo
);

  wire comparator_1_eq, comparator_2_eq, comparator_3_eq, comparator_4_eq;

  Comparator #(.width(1)) comparator_1 (.a(A), .b(NA), .eq(comparator_1_eq));  // open: gt, lt
  Comparator #(.width(1)) comparator_2 (.a(B), .b(NB), .eq(comparator_2_eq));  // open: gt, lt
  Comparator #(.width(1)) comparator_3 (.a(C), .b(NC), .eq(comparator_3_eq));  // open: gt, lt
  Comparator #(.width(1)) comparator_4 (.a(D), .b(ND), .eq(comparator_4_eq));  // open: gt, lt
  and and_1 (bingo, comparator_1_eq, comparator_2_eq, comparator_3_eq, comparator_4_eq);
endmodule

module Resultado (
  input  in_1,
  input  in_2,
  output acertou,
  output errou
);

  or or_1 (acertou, in_1, in_2);
  not not_1 (errou, acertou);
endmodule
