// Logisim project S3.circ as structural Verilog: 1 circuit, main circuit main
module main (
  input  A,
  input  B,
  input  C,
  input  D,
  output S3
);

  wire and_1_out, and_2_out, and_3_out, and_4_out, not_1_out, not_2_out, not_3_out, or_1_out, or_2_out;

  not not_1 (not_1_out, B);
  not not_2 (not_2_out, C);
  not not_3 (not_3_out, D);
  and and_1 (and_1_out, not_1_out, not_3_out);
  and and_2 (and_2_out, C, not_3_out);
  and and_3 (and_3_out, A, not_1_out, not_2_out);
  and and_4 (and_4_out, A, not_3_out);
  or or_1 (or_1_out, and_1_out, and_2_out);
  or or_2 (or_2_out, and_3_out, and_4_out);
  or or_3 (S3, or_1_out, or_2_out);
endmodule
